// Logisim project my_own_computer.circ as structural Verilog
module my_computer (
  input  in_1,
  input  in_2,
  input  in_3,
  input  in_4,
  input  in_5,
  input  in_6,
  output [15:0] out_7
);

  wire [15:0] MAR_o, ram_1_dout;

  my_reg D (.i(out_7), .s(in_3), .e(in_5), .o(out_7));
  my_reg JR (.i(out_7), .o(out_7));  // open: s, e
  my_reg R0 (.i(out_7), .o(out_7));  // open: s, e
  my_reg R1 (.i(out_7), .o(out_7));  // open: s, e
  my_reg R2 (.i(out_7), .o(out_7));  // open: s, e
  RAM #(.addrWidth(16), .dataWidth(16), .trigger("high")) ram_1 (
    .addr(MAR_o), .we(in_2), .oe(in_4), .din(out_7), .dout(ram_1_dout));
  assign out_7 = in_6 ? ram_1_dout : 16'bz;  // Controlled_Buffer controlled_buffer_1
  my_reg MAR (.i(out_7), .s(in_1), .e(1'b1), .o(MAR_o));
endmodule

module my_reg (
  input  [15:0] i,
  input  s,
  input  e,
  output [15:0] o
);

  wire [15:0] register_1_q;

  Register #(.trigger("high"), .width(16)) register_1 (.D(i), .clk(s), .Q(register_1_q));  // open: en, clr
  assign o = e ? register_1_q : 16'bz;  // Controlled_Buffer controlled_buffer_1
endmodule
